// Logisim project 3.2_BancRegsBiport+PC.circ as structural Verilog: 4 circuits, main circuit main
module main (
);

  BancRegistres4x8b bancregistres4x8b_1 ();  // open: RegIn, NúmRegIn, Wr, Sinc, Reset, RegOut1, RegOut2, NúmRegOut2, NúmRegOut1
  PC8bits pc8bits_1 ();  // open: NewPC, Load, Inc, Sinc, Reset, PCout

  // Notes on the sheet:
  //   PractFC3.2 Equip AA99$NomA Cognom1A Cognom2A$NomB Cognom1B Cognom2B
endmodule

module BancRegistres4x8b (
  input  [7:0] RegIn,
  input  [1:0] \NúmRegIn ,
  input  Wr,
  input  Sinc,
  input  Reset,
  input  [1:0] \NúmRegOut1 ,
  input  [1:0] \NúmRegOut2 ,
  output [7:0] RegOut1,
  output [7:0] RegOut2
);

  Registre8bits R0 ();  // open: Wr, Sinc, Reset, Din, Dout
  Registre8bits R1 ();  // open: Wr, Sinc, Reset, Din, Dout
  Registre8bits R2 ();  // open: Wr, Sinc, Reset, Din, Dout
  Registre8bits R3 ();  // open: Wr, Sinc, Reset, Din, Dout
endmodule

module PC8bits (
  input  [7:0] NewPC,
  input  Load,
  input  Inc,
  input  Sinc,
  input  Reset,
  output [7:0] PCout
);

  Registre8bits registre8bits_1 ();  // open: Wr, Sinc, Reset, Din, Dout
endmodule

module Registre8bits (
  input  [7:0] Din,
  input  Wr,
  input  Sinc,
  input  Reset,
  output [7:0] Dout
);

  Register #(.Select("low")) Reg8b (.D(Din), .en(Wr), .Q(Dout), .clk(Sinc), .clr(Reset));
endmodule
